# Fritzing sketch Untitled Sketch 2 (saved by Fritzing 0.9.3b)
breadboards: 1

parts:
  Pico_H1 = Raspberry Pi Pico H
  Sensore_PIR_HC-SR502 = HC-SR501 Body Sensor Module
  J1 = Piezo Speaker

nets:
  3V3: Pico_H1.3V3, Sensore_PIR_HC-SR502.VCC
  N1: Pico_H1.AGND, Sensore_PIR_HC-SR502.GND, J1.pin1
  N2: Pico_H1.GP19, Sensore_PIR_HC-SR502.OUT

custom parts:
  Raspberry Pi Pico H: Raspberry Pi Pico H. Based around the RP2040 microcontroller the Pico H is a low cost microcontroller device bringing Raspberry Pi quality, cost, and easy of use to the microcontroller space.
  HC-SR501 Body Sensor Module: Pyroelectric Infrared PIR Motion Sensor Detector Module
