# Fritzing sketch Untitled Sketch 2 (saved by Fritzing 0.9.3b)
breadboards: 1

parts:
  Pico_H1 = Raspberry Pi Pico H
  U1 = POT [package=pot_mammoth]

nets:
  N1: Pico_H1.3V3_EN, U1.S
  N2: Pico_H1.AGND, U1.E
  N3: Pico_H1.GP27_A1, U1.A

notes:
  Kablonun biri kırmızı biri mavi

custom parts:
  Raspberry Pi Pico H: Raspberry Pi Pico H. Based around the RP2040 microcontroller the Pico H is a low cost microcontroller device bringing Raspberry Pi quality, cost, and easy of use to the microcontroller space.
