# Fritzing sketch Untitled Sketch 2 (saved by Fritzing 0.9.3b)
breadboards: 1

parts:
  Pico_H1 = Raspberry Pi Pico H
  LED1 = LED - 5mm [color="Red (633nm)" package="5 mm [THT]"]
  R1 = Resistor [tolerance=±5% resistance=220 package=THT]
  LED2 = LED - 5mm [color="Red (633nm)" package="5 mm [THT]"]  # not connected
  R2 = Resistor [tolerance=±5% resistance=220 package=THT]

nets:
  N1: Pico_H1.GP18, R2.Pin_0
  N2: Pico_H1.GP16, R1.Pin_0
  N3: Pico_H1.GND, LED1.cathode

notes:
  Kablonun biri kırmızı biri mavi

custom parts:
  Raspberry Pi Pico H: Raspberry Pi Pico H. Based around the RP2040 microcontroller the Pico H is a low cost microcontroller device bringing Raspberry Pi quality, cost, and easy of use to the microcontroller space.
