# Fritzing sketch Untitled Sketch 2 (saved by Fritzing 0.9.3b)
breadboards: 1

parts:
  Pico_H1 = Raspberry Pi Pico H
  LED1 = LED - 3mm [color="Red (633nm)" package="3 mm [THT]"]
  R1 = Resistor [tolerance=±5% resistance=220 package="2512 [SMD]"]
  S1 = Pushbutton [package="[SMD]"]

nets:
  N1: Pico_H1.GND, R1.Pin_1
  N2: Pico_H1.3V3, S1.Pin_4
  N3: Pico_H1.GP5, S1.Pin_1, S1.Pin_2
  N4: Pico_H1.GP2, LED1.anode

custom parts:
  Raspberry Pi Pico H: Raspberry Pi Pico H. Based around the RP2040 microcontroller the Pico H is a low cost microcontroller device bringing Raspberry Pi quality, cost, and easy of use to the microcontroller space.
