# Fritzing sketch Untitled Sketch 2 (saved by Fritzing 0.9.3b)
breadboards: 1

parts:
  Pico_H1 = Raspberry Pi Pico H
  U1 = POT [package=pot_mammoth]
  LCM1602_IIC2 = LCM1602 IIC [part_number="LCM1602 IIC" chip_label="LCM1602 IIC" package="DIP (Dual Inline) [THT]"]
  LCD1 = LCD screen  # not connected

nets:
  3V3: Pico_H1.3V3, U1.E, LCM1602_IIC2.VCC
  N1: Pico_H1.AGND, U1.S, LCM1602_IIC2.GND
  N2: Pico_H1.RUN, U1.A
  N3: Pico_H1.GP21, LCM1602_IIC2.SCL
  N4: Pico_H1.GP20, LCM1602_IIC2.SDA

custom parts:
  Raspberry Pi Pico H: Raspberry Pi Pico H. Based around the RP2040 microcontroller the Pico H is a low cost microcontroller device bringing Raspberry Pi quality, cost, and easy of use to the microcontroller space.
  LCM1602 IIC: I2C-Module to use a 1602 or 2004 LCD on with the wire.h libory Serial LCD Modul
